# Fritzing sketch intval_3_prototype (saved by Fritzing 0.9.3b)
circuit board: 8.46667cm x 5.64444cm
breadboards: 1

parts:
  J1 = Screw terminal - 2 pins [package=THT]
  J2 = Screw terminal - 2 pins [package=THT]
  J3 = Screw terminal - 2 pins [package=THT]
  J4 = Screw terminal - 2 pins [package=THT]
  Raspberry_Pi_Zero1 = Raspberry Pi Zero
  R1 = Resistor [tolerance=±5% resistance=10k package="0805 [SMD]"]
  R2 = Resistor [tolerance=±5% resistance=10k package="0805 [SMD]"]
  Q1 = NPN-Transistor [package="TO92 [THT]"]
  Q2 = NPN-Transistor [package="TO92 [THT]"]

nets:
  N1: J1.pin1, J2.pin2, J3.pin2, Raspberry_Pi_Zero1.GND, Q1.B, Q2.B
  N2: J1.pin2, Raspberry_Pi_Zero1.5V
  N3: J2.pin1, R1.Pin_1
  N4: J3.pin1, R2.Pin_1
  N5: J4.pin1, Q2.C
  N6: J4.pin2, Q1.C
  N7: Raspberry_Pi_Zero1.GPIO5, R1.Pin_0
  N8: Raspberry_Pi_Zero1.GPIO6, R2.Pin_0
  N9: Raspberry_Pi_Zero1.GPIO13, Q1.E
  N10: Raspberry_Pi_Zero1.GPIO19, Q2.E
